# Fritzing sketch Diagrama de fritzing (saved by Fritzing 0.8.7b)

parts:
  Parte1 = Arduino Uno (Rev3)
  L298N1 = L298N DC motor driver
  M2 = DC Motor
  M1 = DC Motor
  Raspberry_Pi_A1 = Raspberry Pi A

nets:
  N1: Parte1.D8, L298N1.IN2
  N2: Parte1.D9_PWM, L298N1.IN1
  N3: Parte1.D10_PWM/SS, L298N1.ENA
  N4: Parte1.D11_PWM/MOSI, Raspberry_Pi_A1.GPIO_11
  N5: Parte1.D12/MISO, Raspberry_Pi_A1.GPIO_9
  N6: Parte1.D13/SCK, Raspberry_Pi_A1.GPIO_10
  GND: Parte1.GND, Raspberry_Pi_A1.GND
  N7: Parte1.D5_PWM, L298N1.ENB
  N8: Parte1.D6_PWM, L298N1.IN4
  N9: Parte1.D7, L298N1.IN3
  N10: L298N1.OUT1, M1.pin_2
  N11: L298N1.OUT2, M1.pin_1
  N12: L298N1.OUT3, M2.pin_2
  N13: L298N1.OUT4, M2.pin_1

custom parts:
  L298N DC motor driver: 2x DC motor driver with 78M05 positive voltage regulator (7..35 V) L298N: max 46 V, 2 A Set 5 V Enable jumper to enable 5 V regultor (needed for the L298N) and +5 V output at screw terminal or supply external +5 V at screw terminal Set ENA and/or ENB to +5 V to enable motor permanently or supply ENA and/or ENB with PWM signal IN1 and IN2 set rotation directory for motor A (OUT1/OUT2) IN2 and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
